// Logisim project alu.circ as structural Verilog: 1 circuit, main circuit alu
module alu (
  input  [31:0] A,
  input  [31:0] B,
  input  [3:0] ALUSel,
  output [31:0] Result
);

  wire comparator_1_lt, comparator_2_eq, xor_2_out;
  wire [31:0] add0, adder_2_out, adder_3_out, adder_4_out, and1, divu8, high, low, mul10, mulh14, mulhu11,
       multiplexer_2_out, multiplexer_4_out, newhigh, not_1_out, not_2_out, not_3_out, or2, remu9, sll6,
       slt7, sra5, srl4, sub12, xor3;

  Adder #(.width(32)) adder_1 (.a(A), .b(B), .out(add0));  // open: cin, cout
  assign and1 = A & B;  // AND_Gate and_1, 32 bits wide
  assign or2 = A | B;  // OR_Gate or_1, 32 bits wide
  assign xor3 = A ^ B;  // XOR_Gate xor_1, 32 bits wide
  Shifter #(.width(32), .shift("lr")) shifter_1 (.in(A), .\dist (B[4:0]), .out(srl4));
  Shifter #(.width(32), .shift("ar")) shifter_2 (.in(A), .\dist (B[4:0]), .out(sra5));
  Shifter #(.width(32)) shifter_3 (.in(A), .\dist (B[4:0]), .out(sll6));
  Multiplexer #(.select(4), .width(32), .enable("false")) multiplexer_1 (
    .in0(add0), .in1(and1), .in2(or2), .in3(xor3), .in4(srl4), .in5(sra5), .in6(sll6), .in7(slt7),
    .in8(divu8), .in9(remu9), .in10(mul10), .in11(mulhu11), .in12(sub12), .in13(B), .in14(mulh14),
    .out(Result), .sel(ALUSel));  // open: in15
  Comparator #(.width(32)) comparator_1 (.a(A), .b(B), .lt(comparator_1_lt));  // open: gt, eq
  Divider #(.width(32)) divider_1 (.a(A), .b(B), .out(divu8), .rem(remu9));  // open: upper
  Multiplier #(.width(32)) multiplier_1 (.a(A), .b(B), .out(mul10), .cout(mulhu11));  // open: cin
  Subtractor #(.width(32)) subtractor_1 (.a(A), .b(B), .out(sub12));  // open: bin, bout
  assign not_1_out = ~A;  // NOT_Gate not_1, 32 bits wide
  assign slt7 = {{31{1'b0}}, comparator_1_lt};  // Bit_Extender bit_extender_1
  Adder #(.width(32)) adder_2 (.a(32'h1), .b(not_1_out), .out(adder_2_out));  // open: cin, cout
  Multiplexer #(.width(32), .enable("false")) multiplexer_2 (
    .in0(A), .in1(adder_2_out), .out(multiplexer_2_out), .sel(A[31]));
  assign not_2_out = ~high;  // NOT_Gate not_2, 32 bits wide
  Adder #(.width(32)) adder_3 (.a(not_2_out), .b(32'h1), .out(adder_3_out));  // open: cin, cout
  assign not_3_out = ~B;  // NOT_Gate not_3, 32 bits wide
  Comparator #(.width(32)) comparator_2 (.a(low), .b({32{1'b0}}), .eq(comparator_2_eq));  // open: gt, lt
  Adder #(.width(32)) adder_4 (.a(32'h1), .b(not_3_out), .out(adder_4_out));  // open: cin, cout
  xor xor_2 (xor_2_out, B[31], A[31]);
  Multiplexer #(.width(32), .enable("false")) multiplexer_3 (
    .in0(not_2_out), .in1(adder_3_out), .out(newhigh), .sel(comparator_2_eq));
  Multiplexer #(.width(32), .enable("false")) multiplexer_4 (
    .in0(B), .in1(adder_4_out), .out(multiplexer_4_out), .sel(B[31]));
  Multiplier #(.width(32)) multiplier_2 (
    .a(multiplexer_2_out), .b(multiplexer_4_out), .out(low), .cout(high));  // open: cin
  Multiplexer #(.width(32), .enable("false")) multiplexer_5 (.in0(high), .in1(newhigh), .out(mulh14), .sel(xor_2_out));

  // Other names for the same wires on the sheet: bsel13[31:0] = B

  // Notes on the sheet:
  //   INPUTS to your circuit
  //   DON'T CHANGE THE LOCATIONS OF THE INPUTS AND OUTPUTS!
  //   OUTPUT from your circuit
endmodule
