// Logisim project cpu.circ as structural Verilog: 3 circuits, main circuit main
module main (
  input  [31:0] INSTRUCTION,
  input  CLOCK,
  output [31:0] PROGRAM_COUNTER,
  output [31:0] ra,
  output [31:0] sp,
  output [31:0] t0,
  output [31:0] t1,
  output [31:0] t2,
  output [31:0] s0,
  output [31:0] s1,
  output [31:0] a0
);

  wire and_1_out, ASEL, B, BrEq, BrLT, BrLTU, BSEL, control_1_out_14, IARI, IJAL, ILOAD, MEMRW,
       multiplexer_11_out, NOP, not_1_out, not_2_out, or_1_out, or_2_out, or_3_out, or_4_out, PCSEL, R,
       REGWEN, S, TAKEN, U, UJ;
  wire [1:0] WBSEL;
  wire [2:0] func3;
  wire [3:0] ALUSEL, ALUSEL_I, ALUSEL_R, multiplexer_15_out;
  wire [4:0] rd, rs1, rs2;
  wire [6:0] func7, opcode;
  wire [7:0] multiplexer_18_out;
  wire [11:0] divider_1_rem, divider_2_rem, immi, imms;
  wire [12:1] immb;
  wire [15:0] multiplexer_19_out;
  wire [19:0] immu;
  wire [20:1] immuj;
  wire [31:0] adder_1_out, adder_2_out, ALU1, ALU2, ALU_result, bit_extender_1_out, bit_extender_2_out,
       bit_extender_3_out, bit_extender_4_out, bit_extender_5_out, bit_extender_6_out, bit_extender_7_out,
       bit_extender_8_out, data1, data2, imm, INSTRUCTION2, MEM_result, multiplexer_1_out, multiplexer_2_out,
       multiplexer_23_out, multiplexer_26_out, multiplexer_27_out, multiplexer_29_out, multiplexer_30_out,
       multiplexer_31_out, multiplexer_32_out, multiplexer_34_out, PROGRAM_COUNTER2, write_data;

  Adder #(.width(32)) adder_1 (.a(PROGRAM_COUNTER), .b(32'h4), .out(adder_1_out));  // open: cin, cout
  Multiplexer #(.width(32), .enable("false")) multiplexer_1 (
    .in0(adder_1_out), .in1(ALU_result), .out(multiplexer_1_out), .sel(PCSEL));
  Register #(.width(32)) PC (.D(multiplexer_1_out), .clk(CLOCK), .Q(PROGRAM_COUNTER));  // open: en, clr
  Comparator #(.width(7)) comparator_1 (.a(INSTRUCTION2[6:0]), .b(7'b0000011), .eq(ILOAD));  // open: gt, lt
  Comparator #(.width(7)) comparator_2 (.a(INSTRUCTION2[6:0]), .b(7'b0010011), .eq(IARI));  // open: gt, lt
  Comparator #(.width(7)) comparator_3 (.a(INSTRUCTION2[6:0]), .b(7'b0110011), .eq(R));  // open: gt, lt
  Comparator #(.width(7)) comparator_4 (.a(INSTRUCTION2[6:0]), .b(7'b0100011), .eq(S));  // open: gt, lt
  Comparator #(.width(7)) comparator_5 (.a(INSTRUCTION2[6:0]), .b(7'b1100011), .eq(B));  // open: gt, lt
  Comparator #(.width(7)) comparator_6 (.a(INSTRUCTION2[6:0]), .b(7'b0110111), .eq(U));  // open: gt, lt
  Comparator #(.width(7)) comparator_7 (.a(INSTRUCTION2[6:0]), .b(7'b1101111), .eq(UJ));  // open: gt, lt
  Comparator #(.width(7)) comparator_8 (.a(INSTRUCTION2[6:0]), .b(7'b1100111), .eq(IJAL));  // open: gt, lt
  Register #(.width(32)) register_1 (.D(PROGRAM_COUNTER), .clk(CLOCK), .Q(PROGRAM_COUNTER2));  // open: en, clr
  Multiplexer #(.width(32), .enable("false")) multiplexer_2 (
    .in0(INSTRUCTION), .in1(32'h13), .out(multiplexer_2_out), .sel(NOP));
  Register #(.width(32)) register_2 (.D(multiplexer_2_out), .clk(CLOCK), .Q(INSTRUCTION2));  // open: en, clr
  Multiplexer #(.width(32), .enable("false")) multiplexer_3 (
    .in1(INSTRUCTION2), .out({immi, rs1, func3, rd, opcode}), .sel(or_1_out));  // open: in0
  or or_1 (or_1_out, IARI, ILOAD, IJAL);
  Multiplexer #(.width(32), .enable("false")) multiplexer_4 (
    .in1(INSTRUCTION2), .out({func7, rs2, rs1, func3, rd, opcode}), .sel(R));  // open: in0
  Multiplexer #(.width(32), .enable("false")) multiplexer_5 (
    .in1(INSTRUCTION2), .out({immu, rd, opcode}), .sel(U));  // open: in0
  Multiplexer #(.width(32), .enable("false")) multiplexer_6 (
    .in1(INSTRUCTION2), .out({imms[11:5], rs2, rs1, func3, imms[4:0], opcode}), .sel(S));  // open: in0
  Multiplexer #(.width(32), .enable("false")) multiplexer_7 (
    .in1(INSTRUCTION2), .out({immuj[20], immuj[10:1], immuj[11], immuj[19:12], rd, opcode}), .sel(UJ));  // open: in0
  Multiplexer #(.width(32), .enable("false")) multiplexer_8 (
    .in1(INSTRUCTION2), .out({immb[12], immb[10:5], rs2, rs1, func3, immb[4:1], immb[11], opcode}), .sel(B));  // open: in0
  not not_1 (not_1_out, BrEq);
  Control control_1 (
    .in_1(ILOAD), .in_2(IARI), .in_3(R), .in_4(S), .in_5(B), .in_6(U), .in_7(UJ), .in_8(IJAL),
    .out_9(REGWEN), .out_10(ASEL), .out_11(BSEL), .out_12(WBSEL), .out_13(MEMRW), .out_14(control_1_out_14));
  Multiplexer #(.enable("false")) multiplexer_9 (.in0(1'b0), .in1(1'b1), .out(NOP), .sel(or_2_out));
  or or_2 (or_2_out, UJ, TAKEN, IJAL);
  Multiplexer #(.enable("false")) multiplexer_10 (.in0(1'b0), .in1(multiplexer_11_out), .out(TAKEN), .sel(B));
  Multiplexer #(.select(3), .enable("false")) multiplexer_11 (
    .in0(BrEq), .in1(not_1_out), .in4(BrLT), .in6(BrLTU), .out(multiplexer_11_out), .sel(func3));  // open: in2, in3, in5, in7
  Multiplexer #(.enable("false")) multiplexer_12 (.in0(control_1_out_14), .in1(1'b1), .out(PCSEL), .sel(TAKEN));
  regfile_main RegFile (
    .rs2(rs2), .rd(rd), .Read_Data_1(data1), .Read_Data_2(data2), .ra(ra), .sp(sp), .t0(t0), .t1(t1),
    .t2(t2), .s0(s0), .s1(s1), .a0(a0), .rs1(rs1), .Write_Data(write_data), .RegWEn(REGWEN), .clk(CLOCK));
  BranchComp branchcomp_1 (.in_1(data1), .in_2(data2), .out_3(BrEq), .out_4(BrLT), .out_5(BrLTU));
  Multiplexer #(.width(32), .enable("false")) multiplexer_13 (
    .in0(data1), .in1(PROGRAM_COUNTER2), .out(ALU1), .sel(ASEL));
  Multiplexer #(.width(32), .enable("false")) multiplexer_14 (.in0(data2), .in1(imm), .out(ALU2), .sel(BSEL));
  Divider #(.width(12)) divider_1 (.a(immi), .b(12'h4), .rem(divider_1_rem));  // open: out, upper
  Divider #(.width(12)) divider_2 (.a(immi), .b(12'h4), .rem(divider_2_rem));  // open: out, upper
  Multiplexer #(.width(4), .enable("false")) multiplexer_15 (
    .in0(4'b0100), .in1(4'b0101), .out(multiplexer_15_out), .sel(immi[10]));
  Multiplexer #(.width(4), .enable("false")) multiplexer_16 (.in1(ALUSEL_I), .out(ALUSEL), .sel(IARI));  // open: in0
  Multiplexer #(.width(4), .enable("false")) multiplexer_17 (.in1(4'b1101), .out(ALUSEL), .sel(U));  // open: in0
  alu Arithmetic_Logic_Unit (.Result(ALU_result), .ALUSel(ALUSEL), .A(ALU1), .B(ALU2));
  Multiplexer #(.select(2), .width(8), .enable("false")) multiplexer_18 (
    .in0(MEM_result[7:0]), .in1(MEM_result[15:8]), .in2(MEM_result[23:16]), .in3(MEM_result[31:24]),
    .out(multiplexer_18_out), .sel(divider_1_rem[1:0]));
  Multiplexer #(.select(2), .width(16), .enable("false")) multiplexer_19 (
    .in0(MEM_result[15:0]), .in2(MEM_result[31:16]), .out(multiplexer_19_out), .sel(divider_2_rem[1:0]));  // open: in1, in3
  Multiplexer #(.select(4), .width(4), .enable("false")) multiplexer_20 (
    .in0(4'b0000), .in1(4'b1010), .in2(4'b0110), .in3(4'b1110), .in4(4'b0111), .in7(4'b1011), .in8(4'b0011),
    .in10(4'b0100), .in11(4'b1000), .in12(4'b0010), .in14(4'b0001), .in15(4'b1001), .out(ALUSEL_R),
    .sel({func3, func7[0]}));  // open: in5, in6, in9, in13
  assign bit_extender_1_out = {{24{multiplexer_18_out[7]}}, multiplexer_18_out};  // Bit_Extender bit_extender_1
  assign bit_extender_2_out = {{16{multiplexer_19_out[15]}}, multiplexer_19_out};  // Bit_Extender bit_extender_2
  Multiplexer #(.select(3), .width(4), .enable("false")) multiplexer_21 (
    .in0(4'b0000), .in1(4'b0110), .in2(4'b0111), .in4(4'b0011), .in5(multiplexer_15_out), .in6(4'b0010),
    .in7(4'b0001), .out(ALUSEL_I), .sel(func3));  // open: in3
  Multiplexer #(.width(4), .enable("false")) multiplexer_22 (
    .in1(4'b1100), .out(ALUSEL_R), .sel(func7[5]));  // open: in0
  Multiplexer #(.select(3), .width(32), .enable("false")) multiplexer_23 (
    .in0(bit_extender_1_out), .in1(bit_extender_2_out), .in2(MEM_result), .out(multiplexer_23_out),
    .sel(func3));  // open: in3, in4, in5, in6, in7
  Multiplexer #(.width(4), .enable("false")) multiplexer_24 (.in1(ALUSEL_R), .out(ALUSEL), .sel(R));  // open: in0
  Multiplexer #(.width(4), .enable("false")) multiplexer_25 (.in1(4'b0000), .out(ALUSEL), .sel(or_3_out));  // open: in0
  or or_3 (or_3_out, S, UJ, B, IJAL);
  Multiplexer #(.width(32), .enable("false")) multiplexer_26 (
    .in0(MEM_result), .in1(multiplexer_23_out), .out(multiplexer_26_out), .sel(ILOAD));
  assign bit_extender_3_out = {{20{imms[11]}}, imms};  // Bit_Extender bit_extender_3
  // mem_main DMEM: pin names not known; wires that end beside it: ALU_result, data2, CLOCK, MEMRW, MEM_result
  Adder #(.width(32)) adder_2 (.a(PROGRAM_COUNTER2), .b(32'h4), .out(adder_2_out));  // open: cin, cout
  Multiplexer #(.width(32), .enable("false")) multiplexer_27 (
    .in0(multiplexer_34_out), .in1(bit_extender_3_out), .out(multiplexer_27_out), .sel(S));
  assign bit_extender_4_out = {{20{immi[11]}}, immi};  // Bit_Extender bit_extender_4
  Multiplexer #(.select(2), .width(32), .enable("false")) multiplexer_28 (
    .in0(ALU_result), .in1(multiplexer_26_out), .in2(adder_2_out), .out(write_data), .sel(WBSEL));  // open: in3
  not not_2 (not_2_out, INSTRUCTION2[13]);
  or or_4 (or_4_out, ILOAD, IJAL);
  and and_1 (and_1_out, INSTRUCTION2[12], not_2_out);
  Multiplexer #(.width(32), .enable("false")) multiplexer_29 (
    .in0(multiplexer_27_out), .in1(bit_extender_4_out), .out(multiplexer_29_out), .sel(or_4_out));
  assign bit_extender_5_out = {{20{INSTRUCTION2[31]}}, INSTRUCTION2[31:20]};  // Bit_Extender bit_extender_5
  assign bit_extender_6_out = {{27{INSTRUCTION2[24]}}, INSTRUCTION2[24:20]};  // Bit_Extender bit_extender_6
  assign bit_extender_7_out = {{11{immuj[20]}}, {immuj, 1'b0}};  // Bit_Extender bit_extender_7
  Multiplexer #(.width(32), .enable("false")) multiplexer_30 (
    .in0(bit_extender_5_out), .in1(bit_extender_6_out), .out(multiplexer_30_out), .sel(and_1_out));
  Multiplexer #(.width(32), .enable("false")) multiplexer_31 (
    .in0(multiplexer_29_out), .in1(bit_extender_7_out), .out(multiplexer_31_out), .sel(UJ));
  assign bit_extender_8_out = {{19{immb[12]}}, {immb, 1'b0}};  // Bit_Extender bit_extender_8
  Multiplexer #(.width(32), .enable("false")) multiplexer_32 (
    .in1(multiplexer_30_out), .out(multiplexer_32_out), .sel(IARI));  // open: in0
  Multiplexer #(.width(32), .enable("false")) multiplexer_33 (
    .in0(multiplexer_31_out), .in1(bit_extender_8_out), .out(imm), .sel(B));
  Multiplexer #(.width(32), .enable("false")) multiplexer_34 (
    .in0(multiplexer_32_out), .in1({immu, {12{1'b0}}}), .out(multiplexer_34_out), .sel(U));

  // Other names for the same wires on the sheet: func7_6 = func7[5]; func7_1 = func7[0]; clk = CLOCK

  // Notes on the sheet:
  //   Output
  //   IMEM (do **NOT** move this)
  //   Inputs
  //   Inputs/Outputs for testing. Do **NOT** move these.
endmodule

module Control (
  input  in_1,
  input  in_2,
  input  in_3,
  input  in_4,
  input  in_5,
  input  in_6,
  input  in_7,
  input  in_8,
  output out_9,
  output out_10,
  output out_11,
  output [1:0] out_12,
  output out_13,
  output out_14
);

  wire or_1_out, or_2_out, or_3_out;
  wire [1:0] multiplexer_3_out;

  Multiplexer #(.enable("false")) multiplexer_1 (.in0(1'b0), .in1(1'b1), .out(out_10), .sel(or_1_out));
  or or_1 (or_1_out, in_7, in_5);
  or or_2 (or_2_out, in_7, in_8);
  Multiplexer #(.enable("false")) multiplexer_2 (.in0(1'b1), .in1(1'b0), .out(out_9), .sel(in_4));
  Multiplexer #(.width(2), .enable("false")) multiplexer_3 (
    .in0(2'b00), .in1(2'b10), .out(multiplexer_3_out), .sel(or_2_out));
  Multiplexer #(.enable("false")) multiplexer_4 (.in0(1'b0), .in1(1'b1), .out(out_14), .sel(or_3_out));
  or or_3 (or_3_out, in_7, in_8);
  Multiplexer #(.width(2), .enable("false")) multiplexer_5 (
    .in0(multiplexer_3_out), .in1(2'b01), .out(out_12), .sel(in_1));
  Multiplexer #(.enable("false")) multiplexer_6 (.in0(1'b1), .in1(1'b0), .out(out_11), .sel(in_3));
  Multiplexer #(.enable("false")) multiplexer_7 (.in0(1'b0), .in1(1'b1), .out(out_13), .sel(in_4));

  // Other names for the same wires on the sheet: ASEL = out_10; B = in_5; BSEL = out_11; IARI = in_2; IJAL = in_8;
  //   ILOAD = in_1; MEMRW = out_13; PCSEL = out_14; R = in_3; REGWEN = out_9; S = in_4; U = in_6; UJ = in_7;
  //   WBSEL[1:0] = out_12
endmodule

module BranchComp (
  input  [31:0] in_1,
  input  [31:0] in_2,
  output out_3,
  output out_4,
  output out_5
);

  Comparator #(.width(32)) comparator_1 (.a(in_1), .b(in_2), .eq(out_3), .lt(out_4));  // open: gt
  Comparator #(.width(32), .mode("unsigned")) comparator_2 (.a(in_1), .b(in_2), .lt(out_5));  // open: gt, eq

  // Other names for the same wires on the sheet: BrEq = out_3; BrLT = out_4; BrLTU = out_5; data1[31:0] = in_1;
  //   data2[31:0] = in_2
endmodule
