// Logisim project cpu.circ as structural Verilog: 1 circuit, main circuit main
module main (
  input  [31:0] INSTRUCTION,
  input  CLOCK,
  output [31:0] PROGRAM_COUNTER,
  output [31:0] ra,
  output [31:0] sp,
  output [31:0] t0,
  output [31:0] t1,
  output [31:0] t2,
  output [31:0] s0,
  output [31:0] s1,
  output [31:0] a0
);

  wire and_1_out, IARI, IJAL, ISTORE, not_1_out, R, S, SB, U, UJ;
  wire [2:0] func3;
  wire [3:0] ALUSEL, multiplexer_3_out;
  wire [4:0] rd, rs1;
  wire [11:0] immi;
  wire [31:0] adder_1_out, adder_2_out, ALU_result, bit_extender_1_out, bit_extender_2_out, data1, imm,
       INSTRUCTION2, MEM_result, multiplexer_6_out, PROGRAM_COUNTER2, write_data;

  Adder #(.width(32)) adder_1 (.a(PROGRAM_COUNTER), .b(32'h4), .out(adder_1_out));  // open: cin, cout
  Register #(.width(32)) PC (.D(adder_1_out), .clk(CLOCK), .Q(PROGRAM_COUNTER));  // open: en, clr
  Comparator #(.width(7)) comparator_1 (.a(INSTRUCTION2[6:0]), .b(7'b0000011), .eq(ISTORE));  // open: gt, lt
  Comparator #(.width(7)) comparator_2 (.a(INSTRUCTION2[6:0]), .b(7'b0010011), .eq(IARI));  // open: gt, lt
  Comparator #(.width(7)) comparator_3 (.a(INSTRUCTION2[6:0]), .b(7'b0110011), .eq(R));  // open: gt, lt
  Comparator #(.width(7)) comparator_4 (.a(INSTRUCTION2[6:0]), .b(7'b0100011), .eq(S));  // open: gt, lt
  Comparator #(.width(7)) comparator_5 (.a(INSTRUCTION2[6:0]), .b(7'b1100011), .eq(SB));  // open: gt, lt
  Comparator #(.width(7)) comparator_6 (.a(INSTRUCTION2[6:0]), .b(7'b0110111), .eq(U));  // open: gt, lt
  Comparator #(.width(7)) comparator_7 (.a(INSTRUCTION2[6:0]), .b(7'b1101111), .eq(UJ));  // open: gt, lt
  Comparator #(.width(7)) comparator_8 (.a(INSTRUCTION2[6:0]), .b(7'b1100111), .eq(IJAL));  // open: gt, lt
  Register #(.width(32)) register_1 (.D(PROGRAM_COUNTER), .clk(CLOCK), .Q(PROGRAM_COUNTER2));  // open: en, clr
  Register #(.width(32)) register_2 (.D(INSTRUCTION), .clk(CLOCK), .Q(INSTRUCTION2));  // open: en, clr
  Multiplexer #(.width(32), .enable("false")) multiplexer_1 (
    .in1(INSTRUCTION2), .out({immi, rs1, func3, rd, INSTRUCTION2[6:0]}), .sel(IARI));  // open: in0
  Multiplexer #(.width(32), .enable("false")) multiplexer_2 (
    .in1(INSTRUCTION2), .out({immi, rs1, func3, rd, INSTRUCTION2[6:0]}), .sel(ISTORE));  // open: in0
  regfile_main RegFile (
    .rd(rd), .Read_Data_1(data1), .ra(ra), .sp(sp), .t0(t0), .t1(t1), .t2(t2), .s0(s0), .s1(s1), .a0(a0),
    .rs1(rs1), .Write_Data(write_data), .RegWEn(1'b1), .clk(CLOCK));  // open: rs2, Read_Data_2
  Multiplexer #(.width(4), .enable("false")) multiplexer_3 (
    .in0(4'b0100), .in1(4'b0101), .out(multiplexer_3_out), .sel(immi[10]));
  Multiplexer #(.select(3), .width(4), .enable("false")) multiplexer_4 (
    .in0(4'b0000), .in1(4'b0110), .in2(4'b0111), .in4(4'b0011), .in5(multiplexer_3_out), .in6(4'b0010),
    .in7(4'b0001), .out(ALUSEL), .sel(func3));  // open: in3
  alu Arithmetic_Logic_Unit (.Result(ALU_result), .ALUSel(ALUSEL), .A(data1), .B(imm));
  Adder #(.width(32)) adder_2 (.a(PROGRAM_COUNTER2), .b(32'h4), .out(adder_2_out));  // open: cin, cout
  not not_1 (not_1_out, INSTRUCTION2[13]);
  Multiplexer #(.select(2), .width(32), .enable("false")) multiplexer_5 (
    .in0(ALU_result), .in1(MEM_result), .in2(adder_2_out), .out(write_data), .sel(2'b00));  // open: in3
  and and_1 (and_1_out, INSTRUCTION2[12], not_1_out);
  Multiplexer #(.width(32), .enable("false")) multiplexer_6 (
    .in1(INSTRUCTION2), .out(multiplexer_6_out), .sel(IARI));  // open: in0
  // mem_main DMEM: pin names not known; wires that end beside it: CLOCK, MEM_result
  assign bit_extender_1_out = {{20{multiplexer_6_out[31]}}, multiplexer_6_out[31:20]};  // Bit_Extender bit_extender_1
  assign bit_extender_2_out = {{27{multiplexer_6_out[24]}}, multiplexer_6_out[24:20]};  // Bit_Extender bit_extender_2
  Multiplexer #(.width(32), .enable("false")) multiplexer_7 (
    .in0(bit_extender_1_out), .in1(bit_extender_2_out), .out(imm), .sel(and_1_out));

  // Other names for the same wires on the sheet: opcode[6:0] = INSTRUCTION2[6:0]; clk = CLOCK

  // Notes on the sheet:
  //   Output
  //   IMEM (do **NOT** move this)
  //   Inputs
  //   Inputs/Outputs for testing. Do **NOT** move these.
endmodule
